# Fritzing sketch esp8266-arduino-nano-PoC (saved by Fritzing 0.9.1b)
breadboards: 1

parts:
  U1 = ESP8266 WiFi Module [part_number=ESP8266]
  Bauteil1 = Arduino Nano (Rev3.0)
  Bauteil2 = Logic Level Converter
  VCC1 = Battery
  USBTTL1 = USB TTL Serial Cable

nets:
  N1: U1.RXD, Bauteil2.TX2_LV
  N2: U1.VCC, U1.CH_PD, Bauteil2.LV, VCC1.+
  GND: U1.GND, Bauteil2.GND, VCC1.-
  N3: U1.TXD, Bauteil2.RX2_LV
  N4: Bauteil1.D1/TX, Bauteil2.TX2_HV
  N5: Bauteil1.D0/RX, Bauteil2.RX2_HV
  N6: Bauteil1.D10, USBTTL1.RX
  N7: Bauteil1.D11/MOSI, USBTTL1.TX
  N8: Bauteil1.5V, Bauteil2.HV

custom parts:
  ESP8266 WiFi Module: Generic WiFi Module based on the ESP8266 with onboard PCB antenna and UART communications
